# Fritzing sketch Schematic (saved by Fritzing 0.9.2b)
breadboards: 1

parts:
  USB = USB connector [package=THT]
  C1 = Electrolytic Capacitor [capacitance=10µF package="100 mil [THT, electrolytic]"]
  R1 = Resistor [tolerance=±5% resistance=220 package=THT]
  R2 = Resistor [tolerance=±5% resistance=1M package=THT]
  R3 = Resistor [tolerance=±5% resistance=68 package=THT]
  R4 = Resistor [tolerance=±5% resistance=1.5k package=THT]
  R5 = Resistor [tolerance=±5% resistance=68 package=THT]
  IC1 = MICROCONTROLLER [part_number=ATMEGA328p package=dil28-3-simon-kit]
  XTAL1 = Crystal [frequency="16 Mhz" package=THT]
  C3 = Ceramic Capacitor [capacitance=22pF package="100 mil [THT, multilayer]"]
  C4 = Ceramic Capacitor [capacitance=22pF package="100 mil [THT, multilayer]"]
  R6 = Resistor [tolerance=±5% resistance=10k package=THT]
  S1 = Pushbutton [package=THT]
  LED1 = LED - 3mm [color="Green (565nm)" package="3 mm [THT]"]
  IC2 = DIP - 16 pins [chip_label=CD4021BE package="DIP (Dual Inline) [THT]"]
  R7 = Resistor [tolerance=±5% resistance=10k package=THT]
  IC3 = DIP - 16 pins [chip_label=CD4021BE package="DIP (Dual Inline) [THT]"]
  S2 = Toggle Switch [package=THT]
  R8 = Resistor [tolerance=±5% resistance=10k package=THT]
  S3 = Toggle Switch [package=THT]
  R9 = Resistor [tolerance=±5% resistance=10k package=THT]
  S4 = Toggle Switch [package=THT]
  R10 = Resistor [tolerance=±5% resistance=10k package=THT]
  S5 = Toggle Switch [package=THT]
  R11 = Resistor [tolerance=±5% resistance=10k package=THT]
  R12 = Resistor [tolerance=±5% resistance=10k package=THT]
  R13 = Resistor [tolerance=±5% resistance=10k package=THT]
  R14 = Resistor [tolerance=±5% resistance=10k package=THT]
  S6 = Toggle Switch [package=THT]
  S7 = Toggle Switch [package=THT]
  S8 = Toggle Switch [package=THT]
  S9 = Toggle Switch [package=THT]
  R15 = Resistor [tolerance=±5% resistance=10k package=THT]
  S10 = Toggle Switch [package=THT]
  R16 = Resistor [tolerance=±5% resistance=10k package=THT]
  R17 = Resistor [tolerance=±5% resistance=10k package=THT]
  R18 = Resistor [tolerance=±5% resistance=10k package=THT]
  S11 = Toggle Switch [package=THT]
  R19 = Resistor [tolerance=±5% resistance=10k package=THT]
  R20 = Resistor [tolerance=±5% resistance=10k package=THT]
  R21 = Resistor [tolerance=±5% resistance=10k package=THT]
  R22 = Resistor [tolerance=±5% resistance=10k package=THT]
  S12 = Toggle Switch [package=THT]
  S13 = Toggle Switch [package=THT]
  D16 = Zener Diode [part_number=3v6 breakdown_voltage=3.6V package="300 mil [THT]"]
  D17 = Zener Diode [part_number=3v6 breakdown_voltage=3.6V package="300 mil [THT]"]
  IC4 = IC, SIP package, 5 pins [chip_label=RE part_number="Rotary Encoder"]
  IC5 = IC, SIP package, 5 pins [chip_label=RE part_number="Rotary Encoder"]
  IC6 = IC, SIP package, 5 pins [chip_label=RE part_number="Rotary Encoder"]
  IC7 = IC, SIP package, 5 pins [chip_label=RE part_number="Rotary Encoder"]
  IC8 = IC, SIP package, 5 pins [chip_label=RE part_number="Rotary Encoder"]

nets:
  5V/VTG: USB.5V, C1.+, R2.Pin_0, R4.Pin_0, IC1.VCC, IC1.AVCC, IC1.AREF, R6.Pin_0, LED1.anode, IC2.pin16, IC3.pin16, S2.COM, S3.COM, S4.COM, S5.COM, S6.COM, S7.COM, S8.COM, S9.COM, S10.COM, S11.COM, S12.COM, S13.COM
  D-: USB.d-, R4.Pin_1, R5.Pin_1, D17.cathode
  D+: USB.d+, R2.Pin_1, R3.Pin_1, D16.cathode
  GND: USB.GND, C1.-, R1.Pin_1, IC1.GND, IC1.AGND, C3.0, C4.0, S1.leg0, IC2.pin8, R7.Pin_1, IC3.pin8, R8.Pin_1, R9.Pin_1, R10.Pin_1, R11.Pin_1, R12.Pin_1, R13.Pin_1, R14.Pin_1, R15.Pin_1, R16.Pin_1, R17.Pin_1, R18.Pin_1, R19.Pin_1, R20.Pin_1, R21.Pin_1, R22.Pin_1, D16.anode, D17.anode, IC4.pin3, IC4.pin4, IC5.pin3, IC5.pin4, IC6.pin3, IC6.pin4, IC7.pin3, IC7.pin4, IC8.pin3, IC8.pin4
  N1: R1.Pin_0, LED1.cathode
  N2: R3.Pin_0, IC1.PD2(INT0)
  N3: R5.Pin_0, IC1.PD3(INT1)
  RESET/RST: IC1.PC6(_RESET), R6.Pin_1, S1.leg1
  REL2: IC1.PD0(RXD), IC6.pin1
  RER2: IC1.PD1(TXD), IC6.pin2
  REL3: IC1.PD4(XCK_T0), IC7.pin1
  N4: IC1.PB6(XTAL1_TOSC1), XTAL1.pin_0, C3.1
  N5: IC1.PB7(XTAL2_TOSC2), XTAL1.pin_1, C4.1
  RER3: IC1.PD5(T1), IC7.pin2
  REL4: IC1.PD6(AIN0), IC8.pin1
  RER4: IC1.PD7(AIN1), IC8.pin2
  REB0: IC1.PB0(ICP), IC4.pin5
  REB1: IC1.PB1(OC1A), IC5.pin5
  REB2: IC1.PB2(SS_OC1B), IC6.pin5
  MOSI/REB3: IC1.PB3(MOSI_OC2), IC7.pin5
  MISO/REB4: IC1.PB4(MISO), IC8.pin5
  REL0/SCK: IC1.PB5(SCK), IC4.pin1
  RER1: IC1.PC0(ADC0), IC5.pin2
  REL1: IC1.PC1(ADC1), IC5.pin1
  RER0: IC1.PC2(ADC2), IC4.pin2
  Clock: IC1.PC3(ADC3), IC2.pin10, IC3.pin10
  Latch: IC1.PC4(ADC4_SDA), IC2.pin9, IC3.pin9
  Data: IC1.PC5(ADC5_SCL), IC2.pin3
  D7: IC2.D7, R13.Pin_0, S9.L1
  D3: IC2.pin4, R10.Pin_0, S5.L1
  D2: IC2.pin5, R9.Pin_0, S4.L1
  D1: IC2.pin6, R8.Pin_0, S3.L1
  D0: IC2.pin7, R7.Pin_0, S2.L1
  N6: IC2.pin11, IC3.pin3
  D4: IC2.pin13, R14.Pin_0, S6.L1
  D5: IC2.pin14, R12.Pin_0, S7.L1
  D6: IC2.pin15, R11.Pin_0, S8.L1
  D15: IC3.D7, R22.Pin_0, S13.L2
  D11: IC3.pin4, R18.Pin_0, S11.L2
  D10: IC3.pin5, R17.Pin_0, S11.L1
  D9: IC3.pin6, S10.L2, R16.Pin_0
  D8: IC3.pin7, R15.Pin_0, S10.L1
  D12: IC3.pin13, R19.Pin_0, S12.L1
  D13: IC3.pin14, R21.Pin_0, S12.L2
  D14: IC3.pin15, R20.Pin_0, S13.L1

notes:
  USB Class B
  GBox Controller rev 2
  ISP6PIN

custom parts:
  DIP - 16 pins: A DIP stand-in part for whatever IC you want. With 16 pins on a 300mil dual inline package (DIP) footprint.
